# Fritzing sketch motor_drivers_robot (saved by Fritzing 0.9.3b)
breadboards: 1

parts:
  VCC1 = 4 x AAA Battery Mount
  M1 = DC Motor
  M2 = DC Motor
  Bauteil1 = Arduino Uno (Rev3)
  Bauteil2 = IFR520 MOS module [package=THT]
  Bauteil3 = IFR520 MOS module [package=THT]
  S1 = Toggle Switch [package=THT]

nets:
  N1: VCC1.-, S1.COM
  N2: VCC1.+, Bauteil1.VIN
  N3: M1.pin_1, Bauteil3.V+
  N4: M1.pin_2, Bauteil3.V-
  N5: M2.pin_1, Bauteil2.V+
  N6: M2.pin_2, Bauteil2.V-
  N7: Bauteil1.D3_PWM, Bauteil2.SIG
  N8: Bauteil1.D6_PWM, Bauteil3.SIG
  VCC: Bauteil1.5V, Bauteil2.VCC, Bauteil3.VCC
  GND: Bauteil1.GND, Bauteil2.GND, Bauteil3.GND, S1.L2
  VIN: Bauteil2.VIN, Bauteil3.VIN
